# Fritzing sketch hidden_device (saved by Fritzing 1.0.0rc)
breadboards: 1

parts:
  part = Arduino Uno Mini LE
  FSR = Basic Force Sensing Resistor (FSR) [package=THT]
  R1 = Resistor [tolerance=±5% power=0.25W resistance=10k part_number=R1 package=THT]
  U1 = ESP8266 ESP-01 Upgraded WiFi Module [part_number=ESP8266]
  R6 = Resistor [tolerance=±5% power=0.25W resistance=10k package=THT]
  R7 = Resistor [tolerance=±5% power=0.25W resistance=10k package=THT]
  R8 = Resistor [tolerance=±5% power=0.25W resistance=10k package=THT]

nets:
  N1: part.A0, FSR.pin_1, R1.Pin_0
  GND: part.GND, R1.Pin_1, U1.GND, R6.Pin_0
  N2: part.D3_PWM, U1.TXD
  N3: part.D5_PWM, R8.Pin_1
  N4: part.D7, part.RESET
  3V3: part.3V3, FSR.pin_2, U1.VCC, U1.CH_PD
  N5: U1.RXD, R7.Pin_1, R8.Pin_0
  N6: R6.Pin_1, R7.Pin_0

custom parts:
  Arduino Uno Mini LE: The UNO Mini Limited Edition (LE) is a miniature version of the classic Arduino UNO board. It is based on the ATmega328P microcontroller, has USB-C connector for programming and powering the board, and pins available for connecting external power sources. It also comes with the standard set of female pin connectors, built-in LED, reset button and everything else that the standard UNO have, but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
  ESP8266 ESP-01 Upgraded WiFi Module: Upgraded Version ESP-01,all Flash are upgraded to 1M byte.Also support Cloud service remote transmission.
